# Fritzing sketch Arduino_FingerIn_doorOpener-PCB-boards (saved by Fritzing 0.9.4)
circuit board: 2.2366cm x 5.35063cm
circuit board: 2.54404cm x 2.82554cm
circuit board: 2.66149cm x 3.02936cm
circuit board: 2.57426cm x 2.85234cm
circuit board: 6.67822cm x 7.33867cm
breadboards: 1

parts:
  Part1 = Arduino Nano (Rev3.0)
  LCD = RJ45 Jack [package=rj45-8]
  Fingerprint = RJ45 Jack [package=rj45-8]
  RFID_sensor = RJ45 Jack [package=rj45-8]
  U7 = RJ45 Jack [package=rj45-8]
  RFID_READER = IC, SIP package, 8 pins [chip_label=RC522]
  U8 = RJ45 Jack [package=rj45-8]
  LCD_16X2_I2C = IC, SIP package, 4 pins [chip_label=IC]
  Relay = RJ45 Jack [package=rj45-8]
  Relay_2 = IC, SIP package, 3 pins [chip_label=IC]
  IC1 = IC, SIP package, 4 pins [chip_label=Connector]
  U9 = RJ45 Jack [package=rj45-8]
  YwRobot_Power_Supply1 = YwRobot Breadboard Power Supply [part_number=545043]
  Relay_3 = RJ45 Jack [package=rj45-8]

nets:
  N1: Part1.GND, LCD.7, Fingerprint.8, YwRobot_Power_Supply1.GND#13, Relay_3.8
  N2: Part1.D2, Fingerprint.2
  N3: Part1.D3, Fingerprint.4
  N4: Part1.D4, Relay_3.6
  N5: Part1.D9, RFID_sensor.8
  N6: Part1.D10, RFID_sensor.6
  N7: Part1.D11/MOSI, RFID_sensor.4
  N8: Part1.D12/MISO, RFID_sensor.2
  N9: Part1.5V, LCD.1, Fingerprint.1, YwRobot_Power_Supply1.VCC#9
  N10: Part1.A5, LCD.4
  N11: Part1.A4, LCD.6
  N12: Part1.D13/SCK, RFID_sensor.1
  N13: RFID_sensor.5, YwRobot_Power_Supply1.GND#11
  N14: RFID_sensor.7, YwRobot_Power_Supply1.VCC#5
  N15: U7.1, RFID_READER.pin2
  N16: U7.2, RFID_READER.pin4
  N17: U7.4, RFID_READER.pin3
  N18: U7.5, RFID_READER.pin6
  N19: U7.6, RFID_READER.pin1
  N20: U7.7, RFID_READER.pin8
  N21: U7.8, RFID_READER.pin7
  N22: U8.1, LCD_16X2_I2C.pin2
  N23: U8.4, LCD_16X2_I2C.pin4
  N24: U8.6, LCD_16X2_I2C.pin3
  N25: U8.7, LCD_16X2_I2C.pin1
  N26: Relay.6, Relay_2.pin1
  N27: Relay.7, Relay_2.pin2
  N28: Relay.8, Relay_2.pin3
  N29: IC1.pin1, U9.1
  N30: IC1.pin2, U9.2
  N31: IC1.pin3, U9.4
  N32: IC1.pin4, U9.8
  N33: YwRobot_Power_Supply1.VCC#10, Relay_3.7

notes:
  Fingerprint
  sensor RJ45
  RFID reader
  LCD
  Relay
  FingerIn

custom parts:
  YwRobot Breadboard Power Supply: The YwRobot Breadboard Power Supply (MB-V2) has two power rails; they can be 5V or 3V3. Power to the module can be provided through the female USB socket or through the A10 (female) 2.1mm power jack.
